// Logisim project FINAL PROJECT.circ as structural Verilog: 15 circuits, main circuit main
module main (
  input  D5,
  input  INP,
  input  CIL,
  input  CIR,
  input  CMA,
  input  load_DR,
  input  add,
  input  \and ,
  input  T4,
  input  T3,
  input  D6,
  input  D4,
  input  T1,
  input  T0,
  input  T2,
  input  D0,
  input  D1,
  input  [3:0] INPR,
  input  D2,
  input  D9,
  input  D15,
  input  D11,
  input  D12,
  input  D13,
  input  D10,
  input  D14,
  input  D3,
  input  D7,
  output E
);

  wire AC_bus, AC_clear, AC_inc, AC_load, ar_1_bus, ar_1_inc, ar_1_load, clock_1_out, DR_bus, DR_load,
       HLT_hlt, IR_bus, IR_load, memory_1_mem_bus, memory_1_mem_ld, OUTR_load, PC_bus, PC_inc, PC_load;
  wire [3:0] AC_2_output, alu_4bit_1_out, AR_2_output, DR_2_output, OUTR_2_output, PC_2_output;
  wire [7:0] controlled_buffer_1_out, n8bit_ir_reg_1_output, ram_1_data;

  AR ar_1 (.T0(T0), .T2(T2), .D5(D5), .T3(T3), .T4(T4), .D4(D4), .LOAD(ar_1_load), .INC(ar_1_inc), .BUS(ar_1_bus));
  pc PC (.D5(D5), .T4(T4), .T3(T3), .D6(D6), .D4(D4), .T1(T1), .T0(T0), .LOAD(PC_load), .INC(PC_inc), .BUS(PC_bus));
  DR DR (.D0(D0), .T3(T3), .D1(D1), .D2(D2), .T4(T4), .LOAD(DR_load), .BUS(DR_bus));
  AC AC (
    .D0(D0), .T4(T4), .D1(D2), .D2(T4), .D9(D9), .T3(T3), .D11(D11), .D12(D12), .D13(D13), .D10(D10),
    .D14(D14), .D3(D3), .D7(D7), .LOAD(AC_load), .INC(AC_inc), .BUS(AC_bus), .CLEAR(AC_clear));
  IR IR (.T1(T1), .T2(T2), .LOAD(IR_load), .BUS(IR_bus));
  OUTR OUTR (.D14(D14), .T3(T3), .LOAD(OUTR_load));
  HLT HLT (.D15(D15), .T3(T3), .HLT(HLT_hlt));
  MEMORY memory_1 (
    .T1(T1), .D0(D0), .T3(T3), .D1(D1), .D2(D2), .D6(D6), .D3(D3), .D5(D5), .MEM_BUS(memory_1_mem_bus),
    .MEM_LD(memory_1_mem_ld));
  ALU_4bit alu_4bit_1 (
    .AC(AC_2_output), .DR(DR_2_output), .INPR(INPR), .AND(\and ), .ADD(add), .LOAD_DR(load_DR), .CMA(CMA),
    .CIR(CIR), .CIL(CIL), .INP(INP), .COUT(E), .OUT(alu_4bit_1_out));  // open: CIN
  Clock clock_1 (.out(clock_1_out));
  RAM #(.addrWidth(4), .bus("separate")) ram_1 (
    .addr(AR_2_output), .din(controlled_buffer_1_out), .data(ram_1_data), .str(memory_1_mem_ld),
    .clk(clock_1_out), .clr(HLT_hlt));  // open: sel, ld
  // Probe on AR_2_output
  _4bit_Reg AR_2 (
    .\input (controlled_buffer_1_out[3:0]), .clock(clock_1_out), .load(ar_1_load), .inc(ar_1_inc),
    .clear(HLT_hlt), .\output (AR_2_output));
  _4bit_Reg PC_2 (
    .\input (controlled_buffer_1_out[3:0]), .clock(clock_1_out), .load(PC_load), .inc(PC_inc),
    .clear(HLT_hlt), .\output (PC_2_output));
  _4bit_Reg DR_2 (
    .\input (controlled_buffer_1_out[3:0]), .clock(clock_1_out), .load(DR_load), .clear(HLT_hlt),
    .\output (DR_2_output));  // open: inc
  AC_Reg AC_2 (
    .\input (alu_4bit_1_out), .clock(clock_1_out), .load(AC_load), .inc(AC_inc), .clear(AC_clear),
    .HLT(HLT_hlt), .\output (AC_2_output));
  _8bit_IR_Reg u_8bit_ir_reg_1 (
    .load(IR_load), .\input (controlled_buffer_1_out), .clock(clock_1_out), .clear(HLT_hlt),
    .\output (n8bit_ir_reg_1_output));
  _4bit_Reg OUTR_2 (
    .\input (controlled_buffer_1_out[3:0]), .clock(clock_1_out), .load(OUTR_load), .clear(HLT_hlt),
    .\output (OUTR_2_output));  // open: inc
  // Probe on PC_2_output
  // Probe on DR_2_output
  // Probe on AC_2_output
  // Probe on n8bit_ir_reg_1_output
  // Probe on OUTR_2_output
  assign controlled_buffer_1_out = ar_1_bus ? {4'b0000, AR_2_output} : 8'bz;  // Controlled_Buffer controlled_buffer_1
  assign controlled_buffer_1_out = DR_bus ? {4'b0000, DR_2_output} : 8'bz;  // Controlled_Buffer controlled_buffer_2
  assign controlled_buffer_1_out = PC_bus ? {4'b0000, PC_2_output} : 8'bz;  // Controlled_Buffer controlled_buffer_3
  assign controlled_buffer_1_out = AC_bus ? {4'b0000, AC_2_output} : 8'bz;  // Controlled_Buffer controlled_buffer_4
  assign controlled_buffer_1_out = IR_bus ? n8bit_ir_reg_1_output : 8'bz;  // Controlled_Buffer controlled_buffer_5
  assign controlled_buffer_1_out = memory_1_mem_bus ? ram_1_data : 8'bz;  // Controlled_Buffer controlled_buffer_6
  // also tied to GND on the sheet: {controlled_buffer_1_out[4], controlled_buffer_1_out[5], controlled_buffer_1_out[6], controlled_buffer_1_out[7]}
endmodule

module _4bit_Reg (
  input  inc,
  input  load,
  input  [3:0] \input ,
  input  clock,
  input  clear,
  output [3:0] \output 
);

  wire and_1_out, and_2_out, and_3_out, and_4_out, and_5_out, and_6_out, and_7_out, and_8_out, and_9_out,
       and_10_out, and_11_out, and_12_out, not_1_out, not_2_out, not_3_out, not_4_out, not_5_out, not_6_out,
       or_1_out, or_2_out, or_3_out, or_4_out, or_5_out, or_6_out, or_7_out, or_8_out;

  not not_1 (not_1_out, load);
  not not_2 (not_2_out, \input [1]);
  not not_3 (not_3_out, \input [2]);
  not not_4 (not_4_out, \input [3]);
  and and_1 (and_1_out, inc, not_1_out);
  not not_5 (not_5_out, not_1_out);
  not not_6 (not_6_out, \input [0]);
  and and_2 (and_2_out, not_5_out, \input [0]);
  and and_3 (and_3_out, not_5_out, not_6_out);
  and and_4 (and_4_out, not_5_out, \input [1]);
  and and_5 (and_5_out, not_2_out, not_5_out);
  and and_6 (and_6_out, not_5_out, \input [2]);
  and and_7 (and_7_out, not_5_out, not_3_out);
  and and_8 (and_8_out, \input [3], not_5_out);
  and and_9 (and_9_out, not_5_out, not_4_out);
  and and_10 (and_10_out, \output [0], and_1_out);
  and and_11 (and_11_out, \output [1], \output [0], and_1_out);
  and and_12 (and_12_out, \output [2], \output [1], \output [0], and_1_out);
  or or_1 (or_1_out, and_2_out, and_1_out);
  or or_2 (or_2_out, and_1_out, and_3_out);
  or or_3 (or_3_out, and_4_out, and_10_out);
  or or_4 (or_4_out, and_10_out, and_5_out);
  or or_5 (or_5_out, and_6_out, and_11_out);
  or or_6 (or_6_out, and_11_out, and_7_out);
  or or_7 (or_7_out, and_8_out, and_12_out);
  or or_8 (or_8_out, and_12_out, and_9_out);
  J_K_Flip_Flop j_k_ff_1 (
    .J(or_1_out), .clk(clock), .K(or_2_out), .Q(\output [0]), .reset(clear));  // open: Qn, preset, en
  J_K_Flip_Flop j_k_ff_2 (
    .J(or_3_out), .clk(clock), .K(or_4_out), .Q(\output [1]), .reset(clear));  // open: Qn, preset, en
  J_K_Flip_Flop j_k_ff_3 (
    .J(or_5_out), .clk(clock), .K(or_6_out), .Q(\output [2]), .reset(clear));  // open: Qn, preset, en
  J_K_Flip_Flop j_k_ff_4 (
    .J(or_7_out), .clk(clock), .K(or_8_out), .Q(\output [3]), .reset(clear));  // open: Qn, preset, en
endmodule

// IR
module _8bit_IR_Reg (
  input  load,
  input  [7:0] \input ,
  input  clock,
  input  clear,
  output [7:0] \output 
);

  _4bit_Reg u_4bit_reg_1 (
    .\input (\input [3:0]), .clock(clock), .load(load), .clear(clear), .\output (\output [3:0]));  // open: inc
  _4bit_Reg u_4bit_reg_2 (
    .\input (\input [7:4]), .clock(clock), .load(load), .clear(clear), .\output (\output [7:4]));  // open: inc
endmodule

module ALU (
  input  INPR,
  input  AC,
  input  DR,
  input  \and ,
  input  add,
  input  Cin,
  input  Id_DR,
  input  cma,
  input  cir,
  input  in_10,
  input  cil,
  input  in_12,
  input  ld_inp,
  output Cout,
  output OUT
);

  wire ADD_out, adder_1_out, and_1_out, AND_2_out, CIL_out, CIR_out, CMA_out, LD_DR_out, LD_INP_out,
       not_1_out;

  and and_1 (and_1_out, DR, AC);
  Adder #(.width(1)) adder_1 (.a(DR), .b(AC), .out(adder_1_out), .cin(Cin), .cout(Cout));
  not not_1 (not_1_out, AC);
  and AND_2 (AND_2_out, \and , and_1_out);
  and u_ADD (ADD_out, add, adder_1_out);
  and LD_DR (LD_DR_out, Id_DR, DR);
  and u_CMA (CMA_out, cma, not_1_out);
  and u_CIR (CIR_out, cir, in_10);
  and u_CIL (CIL_out, cil, in_12);
  and u_LD_INP (LD_INP_out, ld_inp, INPR);
  or or_1 (OUT, AND_2_out, ADD_out, LD_DR_out, CMA_out, CIR_out, CIL_out, LD_INP_out);
endmodule

// ALU
module ALU_4bit (
  input  AND,
  input  ADD,
  input  LOAD_DR,
  input  CMA,
  input  CIR,
  input  CIL,
  input  INP,
  input  CIN,
  input  [3:0] AC,
  input  [3:0] DR,
  input  [3:0] INPR,
  output COUT,
  output [3:0] OUT
);

  wire alu_1_cout, alu_2_cout, alu_3_cout, undriven, undriven_2;

  ALU alu_1 (
    .\and (AND), .add(ADD), .Id_DR(LOAD_DR), .cma(CMA), .cir(CIR), .in_10(undriven_2), .cil(CIL),
    .in_12(undriven), .ld_inp(INP), .INPR(INPR[0]), .AC(AC[0]), .DR(DR[0]), .Cin(CIN), .Cout(alu_1_cout),
    .OUT(OUT[0]));
  ALU alu_2 (
    .\and (AND), .add(ADD), .Id_DR(LOAD_DR), .cma(CMA), .cir(CIR), .in_10(undriven_2), .cil(CIL),
    .in_12(undriven), .ld_inp(INP), .INPR(INPR[1]), .AC(AC[1]), .DR(DR[1]), .Cin(alu_1_cout),
    .Cout(alu_2_cout), .OUT(OUT[1]));
  ALU alu_3 (
    .\and (AND), .add(ADD), .Id_DR(LOAD_DR), .cma(CMA), .cir(CIR), .in_10(undriven_2), .cil(CIL),
    .in_12(undriven), .ld_inp(INP), .INPR(INPR[2]), .AC(AC[2]), .DR(DR[2]), .Cin(alu_2_cout),
    .Cout(alu_3_cout), .OUT(OUT[2]));
  ALU alu_4 (
    .\and (AND), .add(ADD), .Id_DR(LOAD_DR), .cma(CMA), .cir(CIR), .in_10(undriven_2), .cil(CIL),
    .in_12(undriven), .ld_inp(INP), .INPR(INPR[3]), .AC(AC[3]), .DR(DR[3]), .Cin(alu_3_cout), .Cout(COUT),
    .OUT(OUT[3]));
endmodule

module pc (
  input  D5,
  input  T4,
  input  T3,
  input  D6,
  input  D4,
  input  T1,
  input  T0,
  output LOAD,
  output INC,
  output BUS
);

  wire and_1_out, and_2_out, and_3_out, or_1_out;

  and and_1 (and_1_out, D5, T4);
  or or_1 (or_1_out, D6, D4);
  and and_2 (and_2_out, D5, T3);
  and and_3 (and_3_out, T3, or_1_out);
  or or_2 (LOAD, and_1_out, and_3_out);
  or or_3 (BUS, and_2_out, T0);

  assign INC = T1;
endmodule

module DR (
  input  D0,
  input  T3,
  input  D1,
  input  D2,
  input  T4,
  output LOAD,
  output BUS
);

  wire and_1_out, and_2_out, and_3_out;

  and and_1 (and_1_out, D0, T3);
  and and_2 (and_2_out, T3, D1);
  and and_3 (and_3_out, T3, D2);
  and and_4 (BUS, D2, T4);
  or or_1 (LOAD, and_1_out, and_2_out, and_3_out);
endmodule

module AC (
  input  D0,
  input  T4,
  input  D1,
  input  D2,
  input  D9,
  input  T3,
  input  D11,
  input  D12,
  input  D13,
  input  D10,
  input  D14,
  input  D3,
  input  D7,
  output LOAD,
  output INC,
  output BUS,
  output CLEAR
);

  wire and_1_out, and_2_out, and_3_out, and_4_out, and_5_out, and_6_out, and_7_out, and_9_out, and_10_out;

  and and_1 (and_1_out, D0, T4);
  and and_2 (and_2_out, T4, D1);
  and and_3 (and_3_out, T4, D2);
  and and_4 (and_4_out, T3, D9);
  and and_5 (and_5_out, T3, D11);
  and and_6 (and_6_out, T3, D12);
  and and_7 (and_7_out, T3, D13);
  and and_8 (INC, T3, D10);
  and and_9 (and_9_out, T3, D14);
  and and_10 (and_10_out, T3, D3);
  and and_11 (CLEAR, D7, T3);
  or or_1 (BUS, and_9_out, and_10_out);
  or or_2 (LOAD, and_1_out, and_2_out, and_3_out, and_4_out, and_5_out, and_6_out, and_7_out);
endmodule

module AR (
  input  T0,
  input  T2,
  input  D5,
  input  T3,
  input  T4,
  input  D4,
  output LOAD,
  output INC,
  output BUS
);

  wire and_1_out, and_2_out;

  and and_1 (and_1_out, T4, D5);
  and and_2 (and_2_out, T3, D4);
  or or_1 (LOAD, T0, T2);
  and and_3 (INC, D5, T3);
  or or_2 (BUS, and_1_out, and_2_out);
endmodule

module IR (
  input  T1,
  input  T2,
  output LOAD,
  output BUS
);


  assign BUS = T2;
  assign LOAD = T1;
endmodule

module OUTR (
  input  D14,
  input  T3,
  output LOAD
);

  and and_1 (LOAD, D14, T3);
endmodule

module INPR (
  input  D13,
  input  T3,
  output BUS
);

  and and_1 (BUS, D13, T3);
endmodule

module MEMORY (
  input  T1,
  input  D0,
  input  T3,
  input  D1,
  input  D2,
  input  D6,
  input  D3,
  input  D5,
  output MEM_BUS,
  output MEM_LD
);

  wire and_1_out, and_2_out, and_3_out, and_4_out, and_5_out, and_6_out;

  and and_1 (and_1_out, D0, T3);
  and and_2 (and_2_out, T3, D1);
  and and_3 (and_3_out, T3, D2);
  and and_4 (and_4_out, T3, D6);
  and and_5 (and_5_out, T3, D3);
  and and_6 (and_6_out, T3, D5);
  or or_1 (MEM_BUS, T1, and_1_out, and_2_out, and_3_out, and_4_out);
  or or_2 (MEM_LD, and_5_out, and_6_out);
endmodule

module AC_Reg (
  input  inc,
  input  load,
  input  [3:0] \input ,
  input  clock,
  input  clear,
  input  HLT,
  output [3:0] \output 
);

  wire and_1_out, and_2_out, and_3_out, and_4_out, and_5_out, and_6_out, and_7_out, and_8_out, and_9_out,
       and_10_out, and_11_out, and_12_out, not_1_out, not_2_out, not_3_out, not_4_out, not_5_out, not_6_out,
       or_1_out, or_2_out, or_3_out, or_4_out, or_5_out, or_6_out, or_7_out, or_8_out, or_9_out;

  not not_1 (not_1_out, load);
  not not_2 (not_2_out, \input [1]);
  not not_3 (not_3_out, \input [2]);
  not not_4 (not_4_out, \input [3]);
  and and_1 (and_1_out, inc, not_1_out);
  not not_5 (not_5_out, not_1_out);
  not not_6 (not_6_out, \input [0]);
  and and_2 (and_2_out, not_5_out, \input [0]);
  and and_3 (and_3_out, not_5_out, not_6_out);
  and and_4 (and_4_out, not_5_out, \input [1]);
  and and_5 (and_5_out, not_2_out, not_5_out);
  and and_6 (and_6_out, not_5_out, \input [2]);
  and and_7 (and_7_out, not_5_out, not_3_out);
  and and_8 (and_8_out, \input [3], not_5_out);
  and and_9 (and_9_out, not_5_out, not_4_out);
  and and_10 (and_10_out, \output [0], and_1_out);
  and and_11 (and_11_out, \output [1], \output [0], and_1_out);
  and and_12 (and_12_out, \output [2], \output [1], \output [0], and_1_out);
  or or_1 (or_1_out, and_2_out, and_1_out);
  or or_2 (or_2_out, and_1_out, and_3_out);
  or or_3 (or_3_out, and_4_out, and_10_out);
  or or_4 (or_4_out, and_10_out, and_5_out);
  or or_5 (or_5_out, and_6_out, and_11_out);
  or or_6 (or_6_out, and_11_out, and_7_out);
  or or_7 (or_7_out, and_8_out, and_12_out);
  or or_8 (or_8_out, and_12_out, and_9_out);
  J_K_Flip_Flop j_k_ff_1 (
    .J(or_1_out), .clk(clock), .K(or_2_out), .Q(\output [0]), .reset(or_9_out));  // open: Qn, preset, en
  J_K_Flip_Flop j_k_ff_2 (
    .J(or_3_out), .clk(clock), .K(or_4_out), .Q(\output [1]), .reset(or_9_out));  // open: Qn, preset, en
  J_K_Flip_Flop j_k_ff_3 (
    .J(or_5_out), .clk(clock), .K(or_6_out), .Q(\output [2]), .reset(or_9_out));  // open: Qn, preset, en
  J_K_Flip_Flop j_k_ff_4 (
    .J(or_7_out), .clk(clock), .K(or_8_out), .Q(\output [3]), .reset(or_9_out));  // open: Qn, preset, en
  or or_9 (or_9_out, clear, HLT);
endmodule

module HLT (
  input  D15,
  input  T3,
  output HLT
);

  and and_1 (HLT, D15, T3);
endmodule
